// Logisim project pc_simulation.circ as structural Verilog: 1 circuit, main circuit main
module main (
);

  wire adder_1_cout, adder_1_out, adder_2_cout, adder_2_out, adder_3_out, adder_5_cout, adr_CD, adr_inc,
       adr_L, adr_PC, adr_SP, and_1_out, and_2_out, and_4_out, and_5_out, and_6_out, and_7_out, and_10_out,
       and_11_out, and_12_out, and_13_out, and_15_out, and_16_out, and_17_out, and_20_out, and_21_out,
       CARRY_FLAG, clk, clock_1_out, comparator_1_eq, comparator_2_eq, comparator_2_lt, d_ff_1_qn, d_ff_2_q,
       decoder_1_out0, decoder_2_out0, decoder_2_out1, decoder_3_out1, decoder_3_out2, decoder_3_out3,
       decoder_3_out4, decoder_7_out0, decoder_7_out1, decoder_7_out2, decoder_7_out3, decoder_7_out4,
       decoder_7_out5, halt, halted, MINUS_FLAG, not_1_out, not_2_out, not_3_out, not_4_out, not_7_out,
       or_1_out, or_3_out, read_A, read_ALU, read_B, read_C, read_D, read_L1, read_L2, read_MEM, read_PCH,
       read_PCL, read_SPH, read_SPL, RESET, shift_register_1_p5, shift_register_1_p6, shift_register_1_p7,
       shift_register_1_p8, shift_register_1_p9, shift_register_1_p10, shift_register_1_p11,
       shift_register_1_p12, shift_register_1_p13, shift_register_1_p14, shift_register_1_p15,
       shift_register_1_p16, undriven, undriven_2, undriven_3, undriven_4, write_A, write_ALU, write_B,
       write_C, write_D, write_L1, write_L2, write_MEM, write_PC, write_SP, xor_3_out, xor_4_out, ZERO_FLAG;
  wire [2:0] adr_src, data_target, register_2_q;
  wire [3:0] alu_command, data_source;
  wire [4:4] microcode_high_data;
  wire [7:0] adder_5_out, ALU_IN_q, and_14_out, and_19_out, bit_extender_4_out, bit_extender_5_out,
       bit_extender_6_out, data, IR_q, nor_1_out, not_6_out, or_2_out, or_4_out, PROGRAM_data, reg_A_direct,
       REG_B_q, REG_C_q, REG_D_q, reg_L1_direct, REG_L2_q, register_1_q, xor_1_out;
  wire [7:7] microcode_low_data;
  wire [13:11] d_ff_3_q;
  wire [15:0] adder_6_out, address, and_18_out, bit_extender_1_out, bit_extender_2_out, bit_extender_3_out,
       INCR_q, PC_q, register_4_q, SP_q, xor_2_out;
  wire [31:0] adder_4_out, register_3_q;

  Register register_1 (.D(data), .clk(and_2_out), .Q(register_1_q), .clr(RESET));  // open: en
  and and_1 (and_1_out, d_ff_1_qn, clock_1_out);
  Clock clock_1 (.out(clock_1_out));
  Register #(.width(3)) register_2 (
    .D({MINUS_FLAG, ZERO_FLAG, CARRY_FLAG}), .clk(not_1_out), .Q(register_2_q));  // open: en, clr
  not not_1 (not_1_out, clk);
  Register IR (.D(register_1_q), .clk(not_2_out), .Q(IR_q), .clr(RESET));  // open: en
  not not_2 (not_2_out, and_2_out);
  D_Flip_Flop d_ff_1 (.D(halt), .clk(not_3_out), .Q(halted), .Qn(d_ff_1_qn), .reset(RESET));  // open: preset
  not not_3 (not_3_out, and_1_out);
  and and_2 (and_2_out, ~d_ff_3_q[13], ~d_ff_3_q[12], ~d_ff_3_q[11], clk);  // AND_Gate
  D_Flip_Flop d_ff_2 (.D(1'b1), .clk(not_3_out), .Q(d_ff_2_q), .reset(RESET));  // open: Qn, preset
  LED led_1 (.in(halted));
  and and_3 (clk, and_1_out, d_ff_2_q);
  and and_4 (and_4_out, write_MEM, clk);
  Adder #(.width(1)) adder_1 (.a(d_ff_3_q[11]), .b(1'b0), .out(adder_1_out), .cin(1'b1), .cout(adder_1_cout));
  Adder #(.width(1)) adder_2 (.a(d_ff_3_q[12]), .b(1'b0), .out(adder_2_out), .cin(adder_1_cout), .cout(adder_2_cout));
  Adder #(.width(1)) adder_3 (.a(d_ff_3_q[13]), .b(1'b0), .out(adder_3_out), .cin(adder_2_cout));  // open: cout
  ROM #(.addrWidth(14)) microcode_low (
    .addr({d_ff_3_q, register_2_q, IR_q}), .data({microcode_low_data[7], data_target, data_source}));
  ROM #(.addrWidth(14)) microcode_high (
    .addr({d_ff_3_q, register_2_q, IR_q}), .data({adr_src, microcode_high_data[4], alu_command}));
  ROM #(.addrWidth(13)) PROGRAM (.addr(address[12:0]), .data(PROGRAM_data));
  Comparator #(.width(16)) comparator_1 (.a(16'h2000), .b(address), .eq(comparator_1_eq));  // open: gt, lt
  and and_5 (and_5_out, microcode_low_data[7], adder_1_out);
  and and_6 (and_6_out, microcode_low_data[7], adder_2_out);
  and and_7 (and_7_out, microcode_low_data[7], adder_3_out);
  // Shift_Register #(.length(16), .width(8)) shift_register_1: pin names not known; wires that end beside it: RESET, comparator_1_eq, and_4_out, data, shift_register_1_p5, shift_register_1_p6, shift_register_1_p7, shift_register_1_p8, shift_register_1_p9, shift_register_1_p10, shift_register_1_p11, shift_register_1_p12, shift_register_1_p13, shift_register_1_p14, shift_register_1_p15, shift_register_1_p16
  not not_4 (not_4_out, clk);
  D_Flip_Flop d_ff_3 (.D(and_5_out), .clk(not_4_out), .Q(d_ff_3_q[11]), .reset(RESET));  // open: Qn, preset
  D_Flip_Flop d_ff_4 (.D(and_6_out), .clk(not_4_out), .Q(d_ff_3_q[12]), .reset(RESET));  // open: Qn, preset
  D_Flip_Flop d_ff_5 (.D(and_7_out), .clk(not_4_out), .Q(d_ff_3_q[13]), .reset(RESET));  // open: Qn, preset
  assign data = decoder_1_out0 ? PROGRAM_data : 8'bz;  // Controlled_Buffer controlled_buffer_1
  // Probe on shift_register_1_p5
  // Probe on shift_register_1_p6
  // Probe on shift_register_1_p7
  // Probe on shift_register_1_p8
  // Probe on shift_register_1_p9
  // Probe on shift_register_1_p10
  // Probe on shift_register_1_p11
  // Probe on shift_register_1_p12
  // Probe on shift_register_1_p13
  // Probe on shift_register_1_p14
  // Probe on shift_register_1_p15
  // Probe on shift_register_1_p16
  // Probe on undriven
  // Probe on undriven_2
  // Probe on undriven_3
  // Probe on undriven_4
  Decoder #(.select(3)) decoder_1 (
    .out0(decoder_1_out0), .sel(address[15:13]), .en(read_MEM));  // open: out1, out2, out3, out4, out5, out6, out7
  Hex_Digit_Display #(.decimalPoint("false")) hex_digit_display_1 (.value(data[7:4]));
  Decoder #(.select(4)) decoder_2 (
    .out0(decoder_2_out0), .out1(decoder_2_out1), .out8(halt), .sel(alu_command), .en(microcode_high_data[4]));  // open: out2, out3, out4, out5, out6, out7, out9, out10, out11, out12, out13, out14, out15
  Button button_1 (.out(RESET));
  Hex_Digit_Display #(.decimalPoint("false")) hex_digit_display_2 (.value(data[3:0]));
  and and_8 (write_SP, clk, decoder_2_out1);
  and and_9 (write_PC, clk, decoder_2_out0);
  Hex_Digit_Display #(.decimalPoint("false")) hex_digit_display_3 (.value(address[11:8]));
  Hex_Digit_Display #(.decimalPoint("false")) hex_digit_display_4 (.value(address[15:12]));
  Decoder #(.enable("false"), .select(3)) decoder_3 (
    .out1(decoder_3_out1), .out2(decoder_3_out2), .out3(decoder_3_out3), .out4(decoder_3_out4),
    .sel(data_target));  // open: out0, out5, out6, out7
  and and_10 (and_10_out, read_MEM, address[15]);
  and and_11 (and_11_out, address[15], write_MEM);
  LED led_2 (.in(halted));
  Hex_Digit_Display #(.decimalPoint("false")) hex_digit_display_5 (.value(address[7:4]));
  Hex_Digit_Display #(.decimalPoint("false")) hex_digit_display_6 (.value(address[3:0]));
  or or_1 (or_1_out, decoder_3_out1, decoder_3_out2, decoder_3_out3, decoder_3_out4);
  and and_12 (and_12_out, or_1_out, clk);
  RAM #(.addrWidth(15), .asyncread("true"), .databus("bidir"), .\type ("nonvolatile")) ram_1 (
    .addr(address[14:0]), .we(1'b1), .oe(and_10_out), .clk(and_11_out), .data(data));
  Decoder #(.enable("false"), .select(4)) decoder_4 (
    .out1(read_A), .out2(read_B), .out3(read_C), .out4(read_D), .out5(read_L1), .out6(read_L2),
    .out8(read_PCL), .out9(read_PCH), .out10(read_SPL), .out11(read_SPH), .out14(read_ALU), .out15(read_MEM),
    .sel(data_source));  // open: out0, out7, out12, out13
  Register #(.width(32)) register_3 (.D(adder_4_out), .clk(clk), .Q(register_3_q), .clr(RESET));  // open: en
  Adder #(.width(32)) adder_4 (.a(register_3_q), .b(32'h1), .out(adder_4_out));  // open: cin, cout
  Register #(.width(1)) FLAG_Z (.D(comparator_2_eq), .clk(and_12_out), .Q(ZERO_FLAG), .clr(RESET));  // open: en
  Comparator comparator_2 (.a(data), .b({8{1'b0}}), .eq(comparator_2_eq), .lt(comparator_2_lt));  // open: gt
  Register #(.width(1)) FLAG_S (.D(comparator_2_lt), .clk(and_12_out), .Q(MINUS_FLAG), .clr(RESET));  // open: en
  // Probe on register_3_q
  // Probe on clk
  // Probe on data_source
  // Probe on data_target
  // Probe on adr_src
  // Probe on {microcode_high_data[4], alu_command}
  Pull_Resistor #(.pull(1)) pull_resistor_1 (.node(data));
  Pull_Resistor pull_resistor_2 (.node(address));
  Register REG_A (.D(data), .clk(write_A), .Q(reg_A_direct), .clr(RESET));  // open: en
  Register REG_B (.D(data), .clk(write_B), .Q(REG_B_q), .clr(RESET));  // open: en
  Register REG_C (.D(data), .clk(write_C), .Q(REG_C_q), .clr(RESET));  // open: en
  Register REG_D (.D(data), .clk(write_D), .Q(REG_D_q), .clr(RESET));  // open: en
  Register REG_L1 (.D(data), .clk(write_L1), .Q(reg_L1_direct), .clr(RESET));  // open: en
  Register REG_L2 (.D(data), .clk(write_L2), .Q(REG_L2_q), .clr(RESET));  // open: en
  Decoder #(.select(3)) decoder_5 (
    .out0(write_ALU), .out1(write_A), .out2(write_B), .out3(write_C), .out4(write_D), .out5(write_L1),
    .out6(write_L2), .out7(write_MEM), .sel(data_target), .en(clk));
  Decoder #(.enable("false"), .select(3)) decoder_6 (
    .out4(adr_L), .out5(adr_CD), .out6(adr_PC), .out7(adr_SP), .sel(adr_src));  // open: out0, out1, out2, out3
  not not_5 (adr_inc, adr_src[2]);
  assign data = read_A ? reg_A_direct : 8'bz;  // Controlled_Buffer controlled_buffer_2
  assign data = read_B ? REG_B_q : 8'bz;  // Controlled_Buffer controlled_buffer_3
  assign data = read_C ? REG_C_q : 8'bz;  // Controlled_Buffer controlled_buffer_4
  assign data = read_D ? REG_D_q : 8'bz;  // Controlled_Buffer controlled_buffer_5
  assign data = read_L1 ? reg_L1_direct : 8'bz;  // Controlled_Buffer controlled_buffer_6
  assign data = read_L2 ? REG_L2_q : 8'bz;  // Controlled_Buffer controlled_buffer_7
  assign address = adr_CD ? {REG_D_q, REG_C_q} : 16'bz;  // Controlled_Buffer controlled_buffer_8
  assign address = adr_L ? {REG_L2_q, reg_L1_direct} : 16'bz;  // Controlled_Buffer controlled_buffer_9
  Register #(.width(16)) PC (.D(address), .clk(write_PC), .Q(PC_q), .clr(RESET));  // open: en
  Register #(.width(16)) SP (.D(address), .clk(write_SP), .Q(SP_q), .clr(RESET));  // open: en
  Register ALU_IN (.D(data), .clk(write_ALU), .Q(ALU_IN_q));  // open: en, clr
  assign address = adr_PC ? PC_q : 16'bz;  // Controlled_Buffer controlled_buffer_10
  assign data = read_PCL ? PC_q[7:0] : 8'bz;  // Controlled_Buffer controlled_buffer_11
  assign data = read_PCH ? PC_q[15:8] : 8'bz;  // Controlled_Buffer controlled_buffer_12
  assign address = adr_SP ? SP_q : 16'bz;  // Controlled_Buffer controlled_buffer_13
  assign data = read_SPL ? SP_q[7:0] : 8'bz;  // Controlled_Buffer controlled_buffer_14
  assign data = read_SPH ? SP_q[15:8] : 8'bz;  // Controlled_Buffer controlled_buffer_15
  and and_13 (and_13_out, read_ALU, ~alu_command[3]);  // AND_Gate
  assign and_14_out = ALU_IN_q & reg_A_direct;  // AND_Gate and_14, 8 bits wide
  assign or_2_out = ALU_IN_q | reg_A_direct;  // OR_Gate or_2, 8 bits wide
  assign nor_1_out = ~(ALU_IN_q | reg_A_direct);  // NOR_Gate nor_1, 8 bits wide
  assign not_6_out = ~ALU_IN_q;  // NOT_Gate not_6, 8 bits wide
  Decoder #(.select(3)) decoder_7 (
    .out0(decoder_7_out0), .out1(decoder_7_out1), .out2(decoder_7_out2), .out3(decoder_7_out3),
    .out4(decoder_7_out4), .out5(decoder_7_out5), .sel(alu_command[2:0]), .en(and_13_out));  // open: out6, out7
  assign data = decoder_7_out0 ? and_14_out : 8'bz;  // Controlled_Buffer controlled_buffer_16
  assign data = decoder_7_out1 ? or_2_out : 8'bz;  // Controlled_Buffer controlled_buffer_17
  assign data = decoder_7_out2 ? nor_1_out : 8'bz;  // Controlled_Buffer controlled_buffer_18
  assign data = decoder_7_out3 ? not_6_out : 8'bz;  // Controlled_Buffer controlled_buffer_19
  assign data = decoder_7_out4 ? {CARRY_FLAG, ALU_IN_q[7:1]} : 8'bz;  // Controlled_Buffer controlled_buffer_20
  and and_15 (and_15_out, ALU_IN_q[0], decoder_7_out4);
  assign data = decoder_7_out5 ? {ALU_IN_q[6:0], CARRY_FLAG} : 8'bz;  // Controlled_Buffer controlled_buffer_21
  and and_16 (and_16_out, decoder_7_out5, ALU_IN_q[7]);
  Register #(.width(16)) register_4 (.D(address), .clk(clk), .Q(register_4_q));  // open: en, clr
  or or_3 (or_3_out, and_20_out, and_15_out, and_16_out);
  not not_7 (not_7_out, clk);
  and and_17 (and_17_out, read_ALU, clk);
  assign bit_extender_1_out = {{15{adr_src[0]}}, adr_src[0]};  // Bit_Extender bit_extender_1
  assign bit_extender_2_out = {{15{adr_src[1]}}, adr_src[1]};  // Bit_Extender bit_extender_2
  assign bit_extender_3_out = {{8{1'b0}}, reg_L1_direct};  // Bit_Extender bit_extender_3
  Register #(.width(16)) INCR (.D(register_4_q), .clk(not_7_out), .Q(INCR_q));  // open: en, clr
  assign bit_extender_4_out = {{7{alu_command[0]}}, alu_command[0]};  // Bit_Extender bit_extender_4
  assign bit_extender_5_out = {{7{alu_command[1]}}, alu_command[1]};  // Bit_Extender bit_extender_5
  assign bit_extender_6_out = {{7{alu_command[2]}}, alu_command[2]};  // Bit_Extender bit_extender_6
  Register #(.width(1)) FLAG_C (.D(or_3_out), .clk(and_17_out), .Q(CARRY_FLAG));  // open: en, clr
  assign and_18_out = bit_extender_2_out & bit_extender_3_out;  // AND_Gate and_18, 16 bits wide
  assign xor_1_out = ALU_IN_q ^ bit_extender_4_out;  // XOR_Gate xor_1, 8 bits wide
  assign and_19_out = bit_extender_5_out & reg_A_direct;  // AND_Gate and_19, 8 bits wide
  assign xor_2_out = bit_extender_1_out ^ and_18_out;  // XOR_Gate xor_2, 16 bits wide
  assign or_4_out = and_19_out | bit_extender_6_out;  // OR_Gate or_4, 8 bits wide
  xor xor_3 (xor_3_out, adr_src[1], adr_src[0]);
  xor xor_4 (xor_4_out, xor_3_out, 1'b1);
  Adder adder_5 (.a(xor_1_out), .b(or_4_out), .out(adder_5_out), .cin(CARRY_FLAG), .cout(adder_5_cout));
  and and_20 (and_20_out, adder_5_cout, alu_command[3]);
  // Probe on adder_6_out
  Adder #(.width(16)) adder_6 (.a(xor_2_out), .b(INCR_q), .out(adder_6_out), .cin(xor_4_out));  // open: cout
  and and_21 (and_21_out, alu_command[3], read_ALU);
  assign data = and_21_out ? adder_5_out : 8'bz;  // Controlled_Buffer controlled_buffer_22
  assign address = adr_inc ? adder_6_out : 16'bz;  // Controlled_Buffer controlled_buffer_23

  // Other names for the same wires on the sheet: inc_dec = adr_src[0]; inc_offset = adr_src[1]

  // Notes on the sheet:
  //   contents of microcode_low (hex, n*v repeats v):
  //   7*8f 0 7*8f 0 7*8f 0 7*8f 0 7*8f 0 7*8f 0 21*8f 0 0 0 6*8f 0 0 8*8f 8*0 64*8f 16*0 9*8f 0 8f 8f 64*0
  //   11*8f 0 7*8f 0 7*8f 0 7*8f 0 7*8f 0 7*8f 0 21*8f 0 0 0 6*8f 0 0 8*8f 8*0 64*8f 16*0 9*8f 0 8f 8f
  //   64*0 11*8f 0 7*8f 0 7*8f 0 7*8f 0 7*8f 0 7*8f 0 21*8f 0 0 0 6*8f 0 0 8*8f 8*0 64*8f 16*0 9*8f 0 8f
  //   8f 64*0 11*8f 0 7*8f 0 7*8f 0 7*8f 0 7*8f 0 7*8f 0 21*8f 0 0 0 6*8f 0 0 8*8f 8*0 64*8f 16*0 9*8f 0
  //   8f 8f 64*0 11*8f 0 7*8f 0 7*8f 0 7*8f 0 7*8f 0 7*8f 0 21*8f 0 0 0 6*8f 0 0 8*8f 8*0 64*8f 16*0 9*8f
  //   0 8f 8f 64*0 11*8f 0 7*8f 0 7*8f 0 7*8f 0 7*8f 0 7*8f 0 21*8f 0 0 0 6*8f 0 0 8*8f 8*0 64*8f 16*0
  //   9*8f 0 8f 8f 64*0 4*8f 512*0 80 80 80 df ef df df 0 80 80 80 df ef df df 0 80 80 80 df ef df df 0 80
  //   80 80 df ef df df 0 80 80 80 df ef df df 0 80 80 80 df ef df df 0 21*80 0 0 0 80 80 80 ef df df 0 0
  //   8*df 8*0 16*80 4*ef 12*df 4*ef 8*df ef ef df df 4*80 ef ef 4*df ef ef 4*df 16*0 9*ef 0 ef 80 64*0
  //   7*80 df ef df df 0 80 80 80 df ef df df 0 80 80 80 df ef df df 0 80 80 80 df ef df df 0 80 80 80 df
  //   ef df df 0 80 80 80 df ef df df 0 21*80 0 0 0 80 80 80 ef df df 0 0 8*df 8*0 16*80 4*ef 12*df 4*ef
  //   8*df ef ef df df 4*80 ef ef 4*df ef ef 4*df 16*0 9*ef 0 ef 80 64*0 7*80 df ef df df 0 80 80 80 df ef
  //   df df 0 80 80 80 df ef df df 0 80 80 80 df ef df df 0 80 80 80 df ef df df 0 80 80 80 df ef df df 0
  //   21*80 0 0 0 80 80 80 ef df df 0 0 8*df 8*0 16*80 4*ef 12*df 4*ef 8*df ef ef df df 4*80 ef ef 4*df ef
  //   ef 4*df 16*0 9*ef 0 ef 80 64*0 7*80 df ef df df 0 80 80 80 df ef df df 0 80 80 80 df ef df df 0 80
  //   80 80 df ef df df 0 80 80 80 df ef df df 0 80 80 80 df ef df df 0 21*80 0 0 0 80 80 80 ef df df 0 0
  //   8*df 8*0 16*80 4*ef 12*df 4*ef 8*df ef ef df df 4*80 ef ef 4*df ef ef 4*df 16*0 9*ef 0 ef 80 64*0
  //   7*80 df ef df df 0 80 80 80 df ef df df 0 80 80 80 df ef df df 0 80 80 80 df ef df df 0 80 80 80 df
  //   ef df df 0 80 80 80 df ef df df 0 21*80 0 0 0 80 80 80 ef df df 0 0 8*df 8*0 16*80 4*ef 12*df 4*ef
  //   8*df ef ef df df 4*80 ef ef 4*df ef ef 4*df 16*0 9*ef 0 ef 80 64*0 7*80 df ef df df 0 80 80 80 df ef
  //   df df 0 80 80 80 df ef df df 0 80 80 80 df ef df df 0 80 80 80 df ef df df 0 80 80 80 df ef df df 0
  //   21*80 0 0 0 80 80 80 ef df df 0 0 8*df 8*0 16*80 4*ef 12*df 4*ef 8*df ef ef df df 4*80 ef ef 4*df ef
  //   ef 4*df 16*0 9*ef 0 ef 80 64*0 4*80 512*0 82 83 84 80 df 80 80 0 82 83 84 80 df 80 80 0 82 83 84 80
  //   df 80 80 0 82 83 84 80 df 80 80 0 82 83 84 80 df 80 80 0 4*80 df 80 80 0 81 82 83 84 81 82 83 84 81
  //   82 83 84 81 82 83 84 4*81 8e 0 0 0 82 83 84 df 80 80 0 0 8*80 8*0 11 12 13 14 21 22 23 24 31 32 33
  //   34 41 42 43 44 4*df 12*80 4*df 8*80 df df 80 80 0 93 b1 0 df df 4*80 df df 4*80 16*0 9*df 0 df df
  //   64*0 6e 80 0 0 82 83 84 80 df 80 80 0 82 83 84 80 df 80 80 0 82 83 84 80 df 80 80 0 82 83 84 80 df
  //   80 80 0 82 83 84 80 df 80 80 0 4*80 df 80 80 0 81 82 83 84 81 82 83 84 81 82 83 84 81 82 83 84 4*81
  //   8e 0 0 0 82 83 84 df 80 80 0 0 8*80 8*0 11 12 13 14 21 22 23 24 31 32 33 34 41 42 43 44 4*df 12*80
  //   4*df 8*80 df df 80 80 0 93 b1 0 df df 4*80 df df 4*80 16*0 9*df 0 df df 64*0 6e 80 0 0 82 83 84 80
  //   df 80 80 0 82 83 84 80 df 80 80 0 82 83 84 80 df 80 80 0 82 83 84 80 df 80 80 0 82 83 84 80 df 80 80
  //   0 4*80 df 80 80 0 81 82 83 84 81 82 83 84 81 82 83 84 81 82 83 84 4*81 8e 0 0 0 82 83 84 df 80 80 0
  //   0 8*80 8*0 11 12 13 14 21 22 23 24 31 32 33 34 41 42 43 44 4*df 12*80 4*df 8*80 df df 80 80 0 93 b1
  //   0 df df 4*80 df df 4*80 16*0 9*df 0 df df 64*0 6e 80 0 0 82 83 84 80 df 80 80 0 82 83 84 80 df 80 80
  //   0 82 83 84 80 df 80 80 0 82 83 84 80 df 80 80 0 82 83 84 80 df 80 80 0 4*80 df 80 80 0 81 82 83 84
  //   81 82 83 84 81 82 83 84 81 82 83 84 4*81 8e 0 0 0 82 83 84 df 80 80 0 0 8*80 8*0 11 12 13 14 21 22
  //   23 24 31 32 33 34 41 42 43 44 4*df 12*80 4*df 8*80 df df 80 80 0 93 b1 0 df df 4*80 df df 4*80 16*0
  //   9*df 0 df df 64*0 6e 80 0 0 82 83 84 80 df 80 80 0 82 83 84 80 df 80 80 0 82 83 84 80 df 80 80 0 82
  //   83 84 80 df 80 80 0 82 83 84 80 df 80 80 0 4*80 df 80 80 0 81 82 83 84 81 82 83 84 81 82 83 84 81 82
  //   83 84 4*81 8e 0 0 0 82 83 84 df 80 80 0 0 8*80 8*0 11 12 13 14 21 22 23 24 31 32 33 34 41 42 43 44
  //   4*df 12*80 4*df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
  //   contents of microcode_high (hex, n*v repeats v):
  //   7*c0 18 7*c0 18 7*c0 18 7*c0 18 7*c0 18 7*c0 18 21*c0 18 18 18 6*c0 18 18 8*c0 8*18 64*c0 16*18 9*c0
  //   18 c0 c0 64*18 11*c0 18 7*c0 18 7*c0 18 7*c0 18 7*c0 18 7*c0 18 21*c0 18 18 18 6*c0 18 18 8*c0 8*18
  //   64*c0 16*18 9*c0 18 c0 c0 64*18 11*c0 18 7*c0 18 7*c0 18 7*c0 18 7*c0 18 7*c0 18 21*c0 18 18 18 6*c0
  //   18 18 8*c0 8*18 64*c0 16*18 9*c0 18 c0 c0 64*18 11*c0 18 7*c0 18 7*c0 18 7*c0 18 7*c0 18 7*c0 18
  //   21*c0 18 18 18 6*c0 18 18 8*c0 8*18 64*c0 16*18 9*c0 18 c0 c0 64*18 11*c0 18 7*c0 18 7*c0 18 7*c0 18
  //   7*c0 18 7*c0 18 21*c0 18 18 18 6*c0 18 18 8*c0 8*18 64*c0 16*18 9*c0 18 c0 c0 64*18 11*c0 18 7*c0 18
  //   7*c0 18 7*c0 18 7*c0 18 7*c0 18 21*c0 18 18 18 6*c0 18 18 8*c0 8*18 64*c0 16*18 9*c0 18 c0 c0 64*18
  //   4*c0 512*18 10 10 10 4*0 18 10 10 10 4*0 18 10 10 10 4*0 18 10 10 10 4*0 18 10 10 10 4*0 18 10 10 10
  //   4*0 18 21*10 18 18 18 10 10 10 0 0 0 18 18 8*0 8*18 16*10 32*0 4*10 12*0 16*18 9*0 18 0 10 64*18
  //   7*10 4*0 18 10 10 10 4*0 18 10 10 10 4*0 18 10 10 10 4*0 18 10 10 10 4*0 18 10 10 10 4*0 18 21*10 18
  //   18 18 10 10 10 0 0 0 18 18 8*0 8*18 16*10 32*0 4*10 12*0 16*18 9*0 18 0 10 64*18 7*10 4*0 18 10 10
  //   10 4*0 18 10 10 10 4*0 18 10 10 10 4*0 18 10 10 10 4*0 18 10 10 10 4*0 18 21*10 18 18 18 10 10 10 0
  //   0 0 18 18 8*0 8*18 16*10 32*0 4*10 12*0 16*18 9*0 18 0 10 64*18 7*10 4*0 18 10 10 10 4*0 18 10 10 10
  //   4*0 18 10 10 10 4*0 18 10 10 10 4*0 18 10 10 10 4*0 18 21*10 18 18 18 10 10 10 0 0 0 18 18 8*0 8*18
  //   16*10 32*0 4*10 12*0 16*18 9*0 18 0 10 64*18 7*10 4*0 18 10 10 10 4*0 18 10 10 10 4*0 18 10 10 10
  //   4*0 18 10 10 10 4*0 18 10 10 10 4*0 18 21*10 18 18 18 10 10 10 0 0 0 18 18 8*0 8*18 16*10 32*0 4*10
  //   12*0 16*18 9*0 18 0 10 64*18 7*10 4*0 18 10 10 10 4*0 18 10 10 10 4*0 18 10 10 10 4*0 18 10 10 10
  //   4*0 18 10 10 10 4*0 18 21*10 18 18 18 10 10 10 0 0 0 18 18 8*0 8*18 16*10 32*0 4*10 12*0 16*18 9*0
  //   18 0 10 64*18 4*10 512*18 0 0 0 10 0 10 10 18 0 0 0 10 0 10 10 18 0 0 0 10 0 10 10 18 0 0 0 10 0 10
  //   10 18 0 0 0 10 0 10 10 18 0 0 0 10 0 10 10 18 21*0 18 18 18 4*0 10 10 18 18 8*10 8*18 20*0 12*10 4*0
  //   8*10 0 0 10 10 6*0 4*10 0 0 4*10 16*18 9*0 18 0 e0 64*18 0 0 0 18 0 0 0 10 0 10 10 18 0 0 0 10 0 10
  //   10 18 0 0 0 10 0 10 10 18 0 0 0 10 0 10 10 18 0 0 0 10 0 10 10 18 0 0 0 10 0 10 10 18 21*0 18 18 18
  //   4*0 10 10 18 18 8*10 8*18 20*0 12*10 4*0 8*10 0 0 10 10 6*0 4*10 0 0 4*10 16*18 9*0 18 0 e0 64*18 0
  //   0 0 18 0 0 0 10 0 10 10 18 0 0 0 10 0 10 10 18 0 0 0 10 0 10 10 18 0 0 0 10 0 10 10 18 0 0 0 10 0 10
  //   10 18 0 0 0 10 0 10 10 18 21*0 18 18 18 4*0 10 10 18 18 8*10 8*18 20*0 12*10 4*0 8*10 0 0 10 10 6*0
  //   4*10 0 0 4*10 16*18 9*0 18 0 e0 64*18 0 0 0 18 0 0 0 10 0 10 10 18 0 0 0 10 0 10 10 18 0 0 0 10 0 10
  //   10 18 0 0 0 10 0 10 10 18 0 0 0 10 0 10 10 18 0 0 0 10 0 10 10 18 21*0 18 18 18 4*0 10 10 18 18 8*10
  //   8*18 20*0 12*10 4*0 8*10 0 0 10 10 6*0 4*10 0 0 4*10 16*18 9*0 18 0 e0 64*18 0 0 0 18 0 0 0 10 0 10
  //   10 18 0 0 0 10 0 10 10 18 0 0 0 10 0 10 10 18 0 0 0 10 0 10 10 18 0 0 0 10 0 10 10 18 0 0 0 10 0 10
  //   10 18 21*0 18 18 18 4*0 10 10 18 18 8*10 8*18 20*0 12*10 4*0 8*10 0 0 10 10 6*0 4*10 0 0 4*10 16*18
  //   9*0 18 0 e0 64*18 0 0 0 18 0 0 0 10 0 10 10 18 0 0 0 10 0 10 10 18 0 0 0 10 0 10 10 18 0 0 0 10 0 10
  //   10 18 0 0 0 10 0 10 10 18 0 0 0 10 0 10 10 18 21*0 18 18 18 4*0 10 10 18 18 8*10 8*18 20*0 12*10 4*0
  //   8*10 0 0 10 10 6*0 4*10 0 0 4*10 16*18 9*0 18 0 e0 64*18 0 0 0 513*18 a a a 0 10 a0 e0 18 b b b 0 10
  //   a0 e0 18 4*0 10 a0 e0 18 1 1 1 0 10 a0 e0 18 2 2 2 0 10 a0 e0 18 5 5 5 0 10 0 0 18 4*c 4*8 4*9 4*3 5
  //   5 4 4 0 18 18 18 0 0 0 10 a0 e0 18 18 8*e0 8*18 16*0 4*10 4*a0 4*e0 4*0 4*10 4*a0 4*e0 10 10 e0 e0
  //   4*0 10 10 a0 a0 e0 e0 10 10 a0 a0 e0 e0 16*18 9*10 18 10 0 64*18 0 5 0 0 a a a 0 10 a0 e0 18 b b b 0
  //   10 a0 e0 18 4*0 10 a0 e0 18 1 1 1 0 10 a0 e0 18 2 2 2 0 10 a0 e0 18 5 5 5 0 10 0 0 18 4*c 4*8 4*9
  //   4*3 5 5 4 4 0 18 18 18 0 0 0 10 a0 e0 18 18 8*e0 8*18 16*0 4*10 4*a0 4*e0 4*0 4*10 4*a0 4*e0 10 10
  //   e0 e0 4*0 10 10 a0 a0 e0 e0 10 10 a0 a0 e0 e0 16*18 9*10 18 10 0 64*18 0 5 0 0 a a a 0 10 a0 e0 18 b
  //   b b 0 10 a0 e0 18 4*0 10 a0 e0 18 1 1 1 0 10 a0 e0 18 2 2 2 0 10 a0 e0 18 5 5 5 0 10 0 0 18 4*c 4*8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
  //   contents of PROGRAM (hex, n*v repeats v):
  //   9a 1 1 80 20 0 81 20 0 7f b ba 0 17 80 20 0 fc 33 b3 0 b ff 48 fc 0 bb 8165*ff
endmodule
